# Fritzing sketch WiggleBinLight (saved by Fritzing 0.9.10b)
breadboards: 1

parts:
  Power_RGB1 = Prolight RGB 3 Watt Star  # not connected
  R1 = Resistor [tolerance=±5% power=0.25 resistance=1k package=THT]
  R2 = Resistor [tolerance=±5% power=0.25 resistance=10k package=THT]
  Q1S8050 = NPN-Transistor [package="TO92 [THT]"]

nets:
  N1: R1.Pin_0, R2.Pin_1, Q1S8050.C
  N2: R2.Pin_0, Q1S8050.E
